# Fritzing sketch Schema electrica + cod (saved by Fritzing 0.9.10b)

parts:
  L298N1 = L298N DC motor driver
  Part1 = Arduino Uno (Rev3)
  Part2 = Bluetooth HC-05 Macho
  M1 = gear-motor
  M2 = gear-motor
  M3 = gear-motor
  M4 = gear-motor
  BAT1 = BC9VPC [package=bc9vpc]
  U1 = SWITCH-SPST-2 [package=switch-spst-vertical]

nets:
  N1: L298N1.OUT1, M1.pin_1, M4.pin_1
  N2: L298N1.OUT2, M1.pin_2, M4.pin_2
  N3: L298N1.OUT3, M2.pin_2, M3.pin_2
  N4: L298N1.OUT4, M2.pin_1, M3.pin_1
  12V: L298N1.12V, Part1.VIN, U1.P
  GND: L298N1.GND, Part1.GND, Part2.GND, BAT1.V-
  N5: L298N1.IN1, Part1.D10_PWM/SS
  N6: L298N1.IN2, Part1.D11_PWM/MOSI
  N7: L298N1.IN3, Part1.D12/MISO
  N8: L298N1.IN4, Part1.D13/SCK
  N9: Part1.D0/RX, Part2.TXD
  N10: Part1.D1/TX, Part2.RXD
  5V: Part1.5V, Part2.VCC
  N11: BAT1.V+, U1.O

custom parts:
  L298N DC motor driver: 2x DC motor driver with 78M05 positive voltage regulator (7..35 V) L298N: max 46 V, 2 A Set 5 V Enable jumper to enable 5 V regultor (needed for the L298N) and +5 V output at screw terminal or supply external +5 V at screw terminal Set ENA and/or ENB to +5 V to enable motor permanently or supply ENA and/or ENB with PWM signal IN1 and IN2 set rotation directory for motor A (OUT1/OUT2) IN2 and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

// code stored in the sketch: Cod_masina.ino
char t;

void setup() {
  pinMode(13, OUTPUT);   //Forward left motor
  pinMode(12, OUTPUT);   //Backwards left motor
  pinMode(11, OUTPUT);   //Forward right motor
  pinMode(10, OUTPUT);   //Backwards right motor
  Serial.begin(9600);

}

void loop() {
  if (Serial.available()) {
    t = Serial.read();
    Serial.println(t);
  }
  switch (t)
  {
  case 'F': //FORWARD
    digitalWrite(13, HIGH);
    digitalWrite(11, HIGH);
    break;
  case 'B': //BACKWARDS
    digitalWrite(12, HIGH);
    digitalWrite(10, HIGH);
    break;
  case 'L': //LEFT
    digitalWrite(11, HIGH);
    break;
  case 'R': //RIGHT
    digitalWrite(13, HIGH);
    break;
  case 'S': //STOP ALL MOTORS
    digitalWrite(13, LOW);
    digitalWrite(12, LOW);
    digitalWrite(11, LOW);
    digitalWrite(10, LOW);
    break;
  }
  delay(100);
}
